# Fritzing sketch Schema (saved by Fritzing 0.9.3b)
breadboards: 1

parts:
  M1 = Stepper Motor - Bipolar
  M2 = Stepper Motor - Bipolar
  U1 = L9110 H-bridge module [part_number="L9110 H-bridge"]
  U2 = L9110 H-bridge module [part_number="L9110 H-bridge"]
  Parte1 = Analog Digital MUX Breakout
  Parte2 = Analog Digital MUX Breakout
  Parte3 = MPR121 Breakout
  Parte4 = MPR121 Breakout
  Parte5 = MPR121 Breakout
  Parte6 = MPR121 Breakout
  Parte7 = MPR121 Breakout
  Parte8 = MPR121 Breakout
  Parte9 = MPR121 Breakout
  Parte10 = MPR121 Breakout
  Parte11 = MPR121 Breakout
  Parte12 = MPR121 Breakout
  J1 = MAGJACK-2 [package=magjack-19938]

nets:
  N1: M1.A, U1.MOTOR_B-B
  N2: M1.C, U1.MOTOR_B-A
  N3: M1.B, U1.MOTOR_A-B
  N4: M1.D, U1.MOTOR_A-A
  N5: M2.A, U2.MOTOR_B-B
  N6: M2.C, U2.MOTOR_B-A
  N7: M2.B, U2.MOTOR_A-B
  N8: M2.D, U2.MOTOR_A-A
  N9: Parte1.C0, Parte3.SCL
  N10: Parte1.C1, Parte4.SCL
  N11: Parte1.C2, Parte5.SCL
  N12: Parte1.C3, Parte6.SCL
  N13: Parte1.C4, Parte7.SCL
  N14: Parte1.C5, Parte8.SCL
  N15: Parte1.C6, Parte9.SCL
  N16: Parte1.C7, Parte10.SCL
  N17: Parte1.C8, Parte11.SCL
  N18: Parte1.C9, Parte12.SCL
  GND: Parte1.GND, Parte2.GND, Parte3.GND, Parte4.GND, Parte5.GND, Parte6.GND, Parte7.GND, Parte8.GND, Parte9.GND, Parte10.GND, Parte12.GND
  3.3V: Parte1.VCC, Parte2.VCC, Parte3.3.3V, Parte4.3.3V, Parte5.3.3V, Parte6.3.3V, Parte7.3.3V, Parte8.3.3V, Parte9.3.3V, Parte10.3.3V, Parte11.3.3V, Parte12.3.3V
  N19: Parte1.S0, Parte2.S0
  N20: Parte1.S1, Parte2.S1
  N21: Parte1.S2, Parte2.S2
  N22: Parte1.S3, Parte2.S3
  N23: Parte2.C0, Parte3.SDA
  N24: Parte2.C1, Parte4.SDA
  N25: Parte2.C2, Parte5.SDA
  N26: Parte2.C3, Parte6.SDA
  N27: Parte2.C4, Parte7.SDA
  N28: Parte2.C5, Parte8.SDA
  N29: Parte2.C6, Parte9.SDA
  N30: Parte2.C7, Parte10.SDA
  N31: Parte2.C8, Parte11.SDA
  N32: Parte2.C9, Parte12.SDA
  N33: J1.SHIELD, J1.GLED-, J1.GLED+, J1.YLED-, J1.YLED+

notes:
  PMOD JA
  TOP
  PMOD JA
  BOTTOM
  Select sensor
  I2C s[3:0]
  PINS:
  IO10
  IO11
  IO12
  IO13
  Cian-SCL
  Pink-SDA
  3.3V
  ethernet
  connection
  ARTY A7
